# Fritzing sketch GTR01 (saved by Fritzing 0.9.2b)

parts:
  Часть2 = Arduino Uno (Rev3)
  Часть3 = SRF05 Ultrasonic Rangefinder
  M2 = DC Motor
  ANT1 = Antenna
  U4 = Control [package=dip08]
  U5 = LIPO-7800mAh
  C1 = GTR Car
  S1 = IR Line Snsor
  S2 = IR Line Snsor
  RC2 = RC Control  # not connected
  Часть5 = Bluetooth HC-06 Macho
  M3 = DC Motor

nets:
  N1: Часть2.D8, U4.B_IN, C1.B_IN
  N2: Часть2.D9_PWM, C1.B_OUT, M3.pin_2
  N3: Часть2.D10_PWM/SS, U4.L_IN, C1.L_IN
  N4: Часть2.D11_PWM/MOSI, M2.pin_2, C1.L_OUT
  N5: Часть2.D12/MISO, U4.R_IN, C1.R_IN
  N6: Часть2.D13/SCK, M2.pin_1, C1.R_OUT
  GND: Часть2.GND, Часть3.GND, U5.-, C1.GND, S1.GND, S2.GND, Часть5.GND
  N7: Часть2.D0/RX, Часть5.TXD
  N8: Часть2.D1/TX, Часть5.RXD
  N9: Часть2.D2, S1.OUT
  N10: Часть2.D3_PWM, S2.OUT
  N11: Часть2.D4, Часть3.Echo
  N12: Часть2.D5_PWM, Часть3.Trig
  N13: Часть2.D6_PWM, U4.F_IN, C1.F_IN
  N14: Часть2.D7, C1.F_OUT, M3.pin_1
  VCC: Часть2.3V3, Часть3.VCC, Часть5.VCC
  VCC_2: Часть2.5V, S1.VCC, S2.VCC
  VIN: Часть2.VIN, U5.+, C1.VIN
  N15: ANT1.antenna_lead, U4.L_OUT, U4.R_OUT, U4.F_OUT, U4.B_OUT

custom parts:
  Control: GTR Control core
  LIPO-7800mAh: 110mAh Lipo-battery
  GTR Car: GTR car 27MHz
  RC Control: Random Wire Antenna
